# Fritzing sketch pinout (saved by Fritzing 0.9.5d)
breadboards: 1

parts:
  A2 = Waveshare e-Paper HAT [package=THT]
  A1 = Raspberry Pi 5
  LED4 = smd LED [color="Red (633nm)" package="0805 [SMD]"]
  R1 = Resistor [tolerance=±5% resistance=220 package=THT]
  Reset = Momentary Switch 6mm 2pin
  Execute = Momentary Switch 6mm 2pin
  Switch_mode = Momentary Switch 6mm 2pin

nets:
  N1: A2.pin_1, A1.GPIO24
  N2: A2.pin_2, A1.GPIO17
  N3: A2.pin_3, A1.GPIO25
  N4: A2.pin_4, A1.GPIO8
  N5: A2.pin_5, A1.GPIO11
  N6: A2.pin_6, A1.GPIO10
  N7: A2.pin_8, A1.3V3
  N8: A1.GND, R1.Pin_0, Reset.1, Execute.1, Switch_mode.1
  N9: A1.GPIO5, Execute.2
  N10: A1.GPIO6, Reset.2
  N11: A1.GPIO16, Switch_mode.2
  N12: A1.GPIO26, LED4.anode
  N13: LED4.cathode, R1.Pin_1

custom parts:
  Waveshare e-Paper HAT: .This is a universal driver board for e-Paper raw panels, can be used to drive various SPI interface e-Paper from Waveshare.
  Raspberry Pi 5: The RPi5, a faster version of the awesome Raspberry Pi4B ARM Board with 40 pin gpio.
  Momentary Switch 6mm 2pin: Momentary Switch 6mm 2 pin Button commonly used for reset or general input.

// code stored in the sketch: pinout.ino

